# Fritzing sketch schematic (saved by Fritzing 0.9.3b)
circuit board: 8.46667cm x 5.64444cm
breadboards: 1

parts:
  IC1 = IC, DIP package, 28 pins [chip_label=IC]
  M1 = Square Pushbutton
  M2 = Square Pushbutton
  M3 = Square Pushbutton
  M4 = Square Pushbutton
  M8 = Square Pushbutton
  M7 = Square Pushbutton
  M6 = Square Pushbutton
  M5 = Square Pushbutton
  M12 = Square Pushbutton
  M11 = Square Pushbutton
  M10 = Square Pushbutton
  m9 = Square Pushbutton
  Display = 7 Segment Display
  S1 = Toggle Switch [package=THT]
  R1 = Rotary Potentiometer (Small) [maximum_resistance=100kΩ package=THT]
  C1 = Ceramic Capacitor [capacitance=100nF package="100 mil [THT, multilayer]"]

nets:
  GND: IC1.pin1, M1.leg0, M2.leg0, M3.leg0, M4.leg0, M8.leg0, M7.leg0, M6.leg0, M5.leg0, M12.leg0, M11.leg0, M10.leg0, m9.leg0, Display.common_anode, S1.COM, R1.leg1, C1.1
  N1: IC1.pin2, M1.leg1
  N2: IC1.pin3, M2.leg1
  N3: IC1.pin4, M3.leg1
  N4: IC1.pin5, M4.leg1
  N5: IC1.pin6, M5.leg1
  N6: IC1.pin7, M6.leg1
  N7: IC1.pin8, M7.leg1
  N8: IC1.pin9, M8.leg1
  N9: IC1.pin10, m9.leg1
  N10: IC1.pin11, M10.leg1
  N11: IC1.pin12, M11.leg1
  N12: IC1.pin13, M12.leg1
  N13: IC1.pin14, Display.Segment_G
  N14: IC1.pin15, Display.Segment_F
  N15: IC1.pin16, Display.Segment_E
  N16: IC1.pin17, Display.Segment_D
  N17: IC1.pin18, Display.Segment_C
  N18: IC1.pin19, Display.Segment_B
  N19: IC1.pin20, Display.Segment_A
  N20: IC1.pin21, S1.L1
  N21: IC1.pin22, S1.L2
  N22: IC1.pin23, R1.wiper, C1.0
  N23: IC1.pin26, R1.leg2
